# Fritzing sketch Wiring Diagram Phase 1 (saved by Fritzing 0.9.2b)
breadboards: 1

parts:
  Part1 = Arduino Mega 2560 (Rev3)
  R1 = Resistor [tolerance=±5% resistance=220 package=THT]
  R3 = Photocell (LDR) [package=THT]
  U1 = Thumb Joystick [package=joystick]
  KY-008_Laserdiode1 = Laser [part_number=1219301 package=keys]
  U2 = LCD-16X2 [package=lcd-16x2]  # not connected
  J1 = Basic Servo
  J2 = female pin header, 2 pins [form="♀ (female)"]
  J3 = female pin header, 2 pins [form="♀ (female)"]
  J4 = female pin header, 2 pins [form="♀ (female)"]
  J5 = female pin header, 2 pins [form="♀ (female)"]

nets:
  N1: Part1.A0, R1.Pin_0, R3.pin_0
  N2: Part1.A1, U1.V-
  N3: Part1.A2, U1.H-
  N4: Part1.D21/SCL, J3.pin1
  N5: Part1.D20/SDA, J2.pin1
  GND: Part1.GND, R1.Pin_1, KY-008_Laserdiode1.connector2pin, J1.gnd, J4.pin1
  N6: Part1.D13_PWM, KY-008_Laserdiode1.connector0pin
  N7: Part1.D9_PWM, J1.pulse
  5V: Part1.5V, R3.pin_1, U1.V, J1.vcc, J5.pin1
  N8: Part1.D2_PWM, U1.H

custom parts:
  Laser: KEYES KY-008 650nm Laser Transmitter Module
