# Fritzing sketch Wiring Diagram (saved by Fritzing 0.9.2b)
breadboards: 2

parts:
  Part2 = Arduino Mega 2560 (Rev3)
  BLUEFRUIT1 = Adafruit Bluefruit EZ-LINK v1.0
  BLUEFRUIT2 = Adafruit Bluefruit EZ-LINK v1.0
  Part3 = Arduino Mega 2560 (Rev3)
  J6 = Basic Servo
  J7 = female pin header, 2 pins [form="♀ (female)"]
  J8 = female pin header, 2 pins [form="♀ (female)"]
  J9 = female pin header, 2 pins [form="♀ (female)"]
  J10 = female pin header, 2 pins [form="♀ (female)"]
  U3 = LCD-16X2 [package=lcd-16x2]  # not connected
  R4 = Resistor [tolerance=±5% resistance=220 package=THT]
  R5 = Photocell (LDR) [package=THT]
  U4 = Thumb Joystick [package=joystick]
  KY-008_Laserdiode3 = Laser [part_number=1219301 package=keys]
  PSU1 = Adjustable Breadboard Power Supply  # not connected
  R6 = Resistor [tolerance=±5% resistance=220 package="2512 [SMD]"]
  Q1 = NPN-Transistor [package="SOT-23 [SMD]"]

nets:
  N1: Part2.D19/RX1, BLUEFRUIT2.Vin
  N2: Part2.D18/TX1, BLUEFRUIT2.TX
  5V: Part2.5V, BLUEFRUIT2.DSR, J6.vcc
  GND: Part2.GND, BLUEFRUIT2.GND, J6.gnd, KY-008_Laserdiode3.connector2pin
  N3: Part2.D22, J6.pulse
  N4: Part2.D23, KY-008_Laserdiode3.connector0pin, R6.Pin_0
  GND_2: BLUEFRUIT1.Sts, BLUEFRUIT1.GND, Part3.GND, J9.pin1, R4.Pin_1
  N5: BLUEFRUIT1.DSR, Part3.5V, J10.pin1, R5.pin_1, U4.V
  N6: Part3.A0, R4.Pin_0, R5.pin_0
  N7: Part3.A1, U4.V-
  N8: Part3.A2, U4.H-
  N9: Part3.D21/SCL, J8.pin1
  N10: Part3.D20/SDA, J7.pin1
  N11: Part3.D2_PWM, U4.H
  N12: R6.Pin_1, Q1.1

custom parts:
  Adafruit Bluefruit EZ-LINK v1.0: Bluefruit EZ-LINK, Bluetooth Serial Link & Arduino Programmer
  Laser: KEYES KY-008 650nm Laser Transmitter Module
